// Logisim project lab1.circ as structural Verilog: 3 circuits, main circuit main
module main (
  input  s,
  input  x,
  input  y,
  output f
);

  wire n7404_1_p2, n7408_1_p3, n7408_2_p3;

  // _7408 7408_1: pin names not known; wires that end beside it: s, y, n7408_1_p3
  // _7404 7404_1: pin names not known; wires that end beside it: s, n7404_1_p2
  // _7408 7408_2: pin names not known; wires that end beside it: n7404_1_p2, x, n7408_2_p3
  // _7432 7432_1: pin names not known; wires that end beside it: n7408_2_p3, n7408_1_p3, f
endmodule

module ex2 (
  input  a,
  input  b,
  input  c,
  input  d,
  output f
);

  wire n7404_1_p3, n7404_1_p5, n7404_1_p7, n7408_1_p3, n7408_1_p6, n7408_1_p9, n7408_1_p10, n7408_1_p11,
       n7408_1_p12, n7408_2_p6, n7432_1_p6, n7432_1_p8, n7432_1_p10;

  // _7404 7404_1: pin names not known; wires that end beside it: a, a, n7404_1_p3, b, n7404_1_p5, c, n7404_1_p7
  // _7408 7408_1: pin names not known; wires that end beside it: n7404_1_p5, n7404_1_p3, n7408_1_p3, n7408_1_p3, d, n7408_1_p6, c, d, n7408_1_p9, n7408_1_p10, n7408_1_p11, n7408_1_p12
  // _7432 7432_1: pin names not known; wires that end beside it: n7408_1_p9, n7404_1_p7, n7408_1_p10, n7408_1_p12, n7408_1_p6, n7432_1_p6, n7432_1_p6, n7432_1_p8, f, n7432_1_p10, n7432_1_p10
  // _7408 7408_2: pin names not known; wires that end beside it: a, n7404_1_p5, n7408_1_p11, a, b, n7408_2_p6, n7408_2_p6, n7404_1_p7, n7432_1_p8

  // Notes on the sheet:
  //   !c+cd
  //   !a!b
  //   !a!bd
  //   a!b(!c+cd)
  //   cd
endmodule

module lab_rev (
  input  a,
  input  c,
  input  b,
  input  d,
  output out_5
);

  wire n7404_1_p2, n7404_1_p4, n7408_1_p3, n7408_1_p6;

  // _7404 7404_1: pin names not known; wires that end beside it: c, n7404_1_p2, b, n7404_1_p4
  // _7408 7408_1: pin names not known; wires that end beside it: a, n7404_1_p2, n7408_1_p3, n7404_1_p4, d, n7408_1_p6
  // _7432 7432_1: pin names not known; wires that end beside it: n7408_1_p3, n7408_1_p6, out_5
endmodule
